// Digital circuit ContDebounce.dig as structural Verilog
module ContDebounce (
  input  bt,
  input  clk,
  input  [3:0] Chave,
  output a,
  output b,
  output c,
  output d,
  output e,
  output f,
  output g,
  output ma,
  output ig,
  output me
);

  wire debounce_1_y, divisor_1_clkout;
  wire [3:0] counter_1_out;

  Divisor divisor_1 (.ClkIn(clk), .div(25'h61a7), .ClkOut(divisor_1_clkout));
  Debounce debounce_1 (.D(bt), .ClkIn(divisor_1_clkout), .y(debounce_1_y));
  Counter #(.Bits(4)) counter_1 (.en(1'b1), .C(debounce_1_y), .clr(1'b0), .out(counter_1_out));  // open: ovf
  Driver7seg driver7seg_1 (.Din(counter_1_out), .a(a), .b(b), .c(c), .d(d), .e(e), .f(f), .g(g));
  Comparator #(.Bits(4)) comparator_1 (.a(counter_1_out), .b(Chave), .gt(ma), .eq(ig), .lt(me));

  // Notes on the sheet:
  //   clk: Hz: 100
endmodule
