// Digital circuit ContSinc4bit.dig as structural Verilog
module ContSinc4bit (
  input  Clr,
  input  CLK,
  output QA,
  output QB,
  output QC,
  output QD
);

  wire and_1_out, and_2_out;

  JK_FF_AS jk_ff_as_1 (.Set(1'b0), .J(and_1_out), .C(CLK), .K(and_1_out), .Clr(Clr), .Q(QD));  // open: nQ
  and and_1 (and_1_out, and_2_out, QC);
  and and_2 (and_2_out, QA, QB);
  JK_FF_AS jk_ff_as_2 (.Set(1'b0), .J(and_2_out), .C(CLK), .K(and_2_out), .Clr(Clr), .Q(QC));  // open: nQ
  JK_FF_AS jk_ff_as_3 (.Set(1'b0), .J(QA), .C(CLK), .K(QA), .Clr(Clr), .Q(QB));  // open: nQ
  JK_FF_AS jk_ff_as_4 (.Set(1'b0), .J(1'b1), .C(CLK), .K(1'b1), .Clr(Clr), .Q(QA));  // open: nQ
endmodule
