// Digital circuit ContSinc4bitDec.dig as structural Verilog
module ContSinc4bitDec (
  input  Clr,
  input  CLK,
  output QA,
  output QB,
  output QC,
  output QD
);

  wire and_1_out, and_2_out, jk_ff_as_2_q, jk_ff_as_3_q, jk_ff_as_4_q;

  JK_FF_AS jk_ff_as_1 (.Set(1'b0), .J(and_1_out), .C(CLK), .K(and_1_out), .Clr(Clr), .nQ(QD));  // open: Q
  and and_1 (and_1_out, and_2_out, jk_ff_as_2_q);
  and and_2 (and_2_out, jk_ff_as_4_q, jk_ff_as_3_q);
  JK_FF_AS jk_ff_as_2 (.Set(1'b0), .J(and_2_out), .C(CLK), .K(and_2_out), .Clr(Clr), .Q(jk_ff_as_2_q), .nQ(QC));
  JK_FF_AS jk_ff_as_3 (.Set(1'b0), .J(jk_ff_as_4_q), .C(CLK), .K(jk_ff_as_4_q), .Clr(Clr), .Q(jk_ff_as_3_q), .nQ(QB));
  JK_FF_AS jk_ff_as_4 (.Set(1'b0), .J(1'b1), .C(CLK), .K(1'b1), .Clr(Clr), .Q(jk_ff_as_4_q), .nQ(QA));
endmodule
