// Digital circuit ContadorDecimal.dig as structural Verilog
module ContadorDecimal (
  input  Rst,
  input  C,
  output QA,
  output QB,
  output QC,
  output QD
);

  wire and_1_out, or_1_out;

  JK_FF_AS jk_ff_as_1 (.Set(1'b0), .J(1'b1), .C(~C), .K(1'b1), .Clr(or_1_out), .Q(QA));  // open: nQ
  or or_1 (or_1_out, Rst, and_1_out);
  JK_FF_AS jk_ff_as_2 (.Set(1'b0), .J(1'b1), .C(~QA), .K(1'b1), .Clr(or_1_out), .Q(QB));  // open: nQ
  JK_FF_AS jk_ff_as_3 (.Set(1'b0), .J(1'b1), .C(~QB), .K(1'b1), .Clr(or_1_out), .Q(QC));  // open: nQ
  JK_FF_AS jk_ff_as_4 (.Set(1'b0), .J(1'b1), .C(~QC), .K(1'b1), .Clr(or_1_out), .Q(QD));  // open: nQ
  and and_1 (and_1_out, QB, QD);
endmodule
