// Digital circuit ContadorHexa.dig as structural Verilog
module ContadorHexa (
  input  Rst,
  input  C,
  output QA,
  output QB,
  output QC,
  output QD
);

  JK_FF_AS jk_ff_as_1 (.Set(1'b0), .J(1'b1), .C(~C), .K(1'b1), .Clr(Rst), .Q(QA));  // open: nQ
  JK_FF_AS jk_ff_as_2 (.Set(1'b0), .J(1'b1), .C(~QA), .K(1'b1), .Clr(Rst), .Q(QB));  // open: nQ
  JK_FF_AS jk_ff_as_3 (.Set(1'b0), .J(1'b1), .C(~QB), .K(1'b1), .Clr(Rst), .Q(QC));  // open: nQ
  JK_FF_AS jk_ff_as_4 (.Set(1'b0), .J(1'b1), .C(~QC), .K(1'b1), .Clr(Rst), .Q(QD));  // open: nQ
endmodule
