// Digital circuit Debounce.dig as structural Verilog
module Debounce (
  input  D,
  input  ClkIn,
  output y
);

  wire d_ff_as_1_nq, d_ff_as_1_q, d_ff_as_2_nq, d_ff_as_2_q, d_ff_as_3_nq, d_ff_as_3_q;

  D_FF_AS d_ff_as_1 (.Set(y), .D(d_ff_as_1_nq), .C(ClkIn), .Clr(~D), .Q(d_ff_as_1_q), .nQ(d_ff_as_1_nq));
  D_FF_AS d_ff_as_2 (.Set(1'b0), .D(d_ff_as_2_nq), .C(d_ff_as_1_nq), .Clr(~D), .Q(d_ff_as_2_q), .nQ(d_ff_as_2_nq));
  D_FF_AS d_ff_as_3 (.Set(1'b0), .D(d_ff_as_3_nq), .C(d_ff_as_2_nq), .Clr(~D), .Q(d_ff_as_3_q), .nQ(d_ff_as_3_nq));
  and and_1 (y, d_ff_as_1_q, d_ff_as_2_q, d_ff_as_3_q);
endmodule
