// Digital circuit Dec7Seg.dig as structural Verilog
module Dec7Seg (
  input  [3:0] D,
  output [6:0] Q
);

  ROM #(.AddrBits(4), .Bits(7)) rom (.A(D), .sel(1'b1), .D(Q));

  // Notes on the sheet:
  //   contents of rom (hex, n*v repeats v):
  //   7e,30,6d,79,33,5b,5f,70,7f,73,77,1f,4e,3d,4f,47
endmodule
