// Digital circuit Div8FF.dig as structural Verilog
module Div8FF (
  input  CLK_in,
  output CLK_out
);

  wire d_ff_1_nq, d_ff_1_q, d_ff_2_nq, d_ff_2_q, d_ff_3_nq, d_ff_3_q, d_ff_4_nq, d_ff_4_q, d_ff_5_nq,
       d_ff_5_q, d_ff_6_nq, d_ff_6_q, d_ff_7_nq, d_ff_7_q, d_ff_8_nq;

  D_FF d_ff_1 (.D(d_ff_1_nq), .C(CLK_in), .Q(d_ff_1_q), .nQ(d_ff_1_nq));
  D_FF d_ff_2 (.D(d_ff_2_nq), .C(d_ff_1_q), .Q(d_ff_2_q), .nQ(d_ff_2_nq));
  D_FF d_ff_3 (.D(d_ff_3_nq), .C(d_ff_2_q), .Q(d_ff_3_q), .nQ(d_ff_3_nq));
  D_FF d_ff_4 (.D(d_ff_4_nq), .C(d_ff_3_q), .Q(d_ff_4_q), .nQ(d_ff_4_nq));
  D_FF d_ff_5 (.D(d_ff_5_nq), .C(d_ff_4_q), .Q(d_ff_5_q), .nQ(d_ff_5_nq));
  D_FF d_ff_6 (.D(d_ff_6_nq), .C(d_ff_5_q), .Q(d_ff_6_q), .nQ(d_ff_6_nq));
  D_FF d_ff_7 (.D(d_ff_7_nq), .C(d_ff_6_q), .Q(d_ff_7_q), .nQ(d_ff_7_nq));
  D_FF d_ff_8 (.D(d_ff_8_nq), .C(d_ff_7_q), .Q(CLK_out), .nQ(d_ff_8_nq));

  // Notes on the sheet:
  //   CLK_in: Hz: 10
endmodule
