// Digital circuit Divisor.dig as structural Verilog
module Divisor (
  input  ClkIn,
  input  [24:0] div,
  output ClkOut
);

  wire comparator_1_eq, d_ff_1_nq;
  wire [24:0] counter_1_out;

  Counter #(.Bits(25)) counter_1 (.en(1'b1), .C(ClkIn), .clr(comparator_1_eq), .out(counter_1_out));  // open: ovf
  Comparator #(.Bits(25)) comparator_1 (.a(counter_1_out), .b(div), .eq(comparator_1_eq));  // open: gt, lt
  D_FF d_ff_1 (.D(d_ff_1_nq), .C(comparator_1_eq), .Q(ClkOut), .nQ(d_ff_1_nq));

  // Notes on the sheet:
  //   ClkIn: Hz: 20
endmodule
