// Digital circuit Driver7seg.dig as structural Verilog
module Driver7seg (
  input  [3:0] Din,
  output a,
  output b,
  output c,
  output d,
  output e,
  output f,
  output g
);

  ROM #(.AddrBits(4), .Bits(7)) rom7seg (.A(Din), .sel(1'b1), .D({g, f, e, d, c, b, a}));

  // Notes on the sheet:
  //   contents of rom7seg (hex, n*v repeats v):
  //   3f,6,5b,4f,66,6d,7d,7,7f,6f,77,7c,39,5e,79,71
endmodule
