// Digital circuit DriverMAX7219HexReg.dig as structural Verilog
module DriverMAX7219HexReg (
  input  CLK,
  input  [3:0] Dig0,
  input  [3:0] Dig1,
  input  [3:0] Dig2,
  input  [3:0] Dig3,
  input  [3:0] Dig4,
  input  [3:0] Dig5,
  input  [3:0] Dig6,
  input  [3:0] Dig7,
  input  [3:0] Brilho,
  output DO,
  output CS,
  output CLKout
);

  wire [3:0] counter_2_out;
  wire [6:0] dec7seg_1_q, dec7seg_2_q, dec7seg_3_q, dec7seg_4_q, dec7seg_5_q, dec7seg_6_q, dec7seg_7_q,
       dec7seg_8_q;
  wire [7:0] multiplexer_1_out;

  Dec7Seg dec7seg_1 (.D(Dig0), .Q(dec7seg_1_q));
  Dec7Seg dec7seg_2 (.D(Dig1), .Q(dec7seg_2_q));
  Dec7Seg dec7seg_3 (.D(Dig2), .Q(dec7seg_3_q));
  Dec7Seg dec7seg_4 (.D(Dig3), .Q(dec7seg_4_q));
  Dec7Seg dec7seg_5 (.D(Dig4), .Q(dec7seg_5_q));
  Dec7Seg dec7seg_6 (.D(Dig5), .Q(dec7seg_6_q));
  Dec7Seg dec7seg_7 (.D(Dig6), .Q(dec7seg_7_q));
  Dec7Seg dec7seg_8 (.D(Dig7), .Q(dec7seg_8_q));
  Counter #(.Bits(4)) counter_1 (.en(1'b1), .C(CLK), .clr(1'b0), .ovf(CS));  // open: out
  Counter #(.Bits(4)) counter_2 (.en(1'b1), .C(CS), .clr(1'b0), .out(counter_2_out));  // open: ovf
  Multiplexer #(.Selector_Bits(4), .Bits(8)) multiplexer_1 (
    .sel(counter_2_out), .in_0({8{1'b0}}), .in_1({1'b0, dec7seg_1_q}), .in_2({1'b0, dec7seg_2_q}),
    .in_3({1'b0, dec7seg_3_q}), .in_4({1'b0, dec7seg_4_q}), .in_5({1'b0, dec7seg_5_q}),
    .in_6({1'b0, dec7seg_6_q}), .in_7({1'b0, dec7seg_7_q}), .in_8({1'b0, dec7seg_8_q}), .in_9({8{1'b0}}),
    .in_10({4'b0000, Brilho}), .in_11(8'h7), .in_12(8'h1), .in_13({8{1'b0}}), .in_14({8{1'b0}}),
    .in_15({8{1'b0}}), .out(multiplexer_1_out));
  RegParSer16 regparser16_1 (.Ld(CS), .Clk(CLK), .Data({4'b0000, counter_2_out, multiplexer_1_out}), .Q(DO));

  assign CLKout = CLK;

  // Notes on the sheet:
  //   CLK: Hz: 1000
endmodule
