// Digital circuit DriverMAX7219_8x8.dig as structural Verilog
module DriverMAX7219_8x8 (
  input  [3:0] Brilho,
  input  [7:0] D,
  input  [2:0] Addr,
  input  CLK,
  output DO,
  output CS,
  output CLKout
);

  wire and_1_out, and_2_out, and_3_out, and_4_out, and_5_out, and_6_out, and_7_out, and_8_out,
       comparator_2_eq, decoder_1_out_0, decoder_1_out_1, decoder_1_out_2, decoder_1_out_3, decoder_1_out_4,
       decoder_1_out_5, decoder_1_out_6, decoder_1_out_7;
  wire [3:0] counter_2_out;
  wire [4:0] counter_1_out;
  wire [7:0] d_ff_1_q, d_ff_2_q, d_ff_3_q, d_ff_4_q, d_ff_5_q, d_ff_6_q, d_ff_7_q, d_ff_8_q,
       multiplexer_1_out;

  Decoder #(.Selector_Bits(3)) decoder_1 (
    .sel(Addr), .out_0(decoder_1_out_0), .out_1(decoder_1_out_1), .out_2(decoder_1_out_2),
    .out_3(decoder_1_out_3), .out_4(decoder_1_out_4), .out_5(decoder_1_out_5), .out_6(decoder_1_out_6),
    .out_7(decoder_1_out_7));
  Counter #(.Bits(5)) counter_1 (.en(1'b1), .C(CLK), .clr(CS), .out(counter_1_out));  // open: ovf
  and and_1 (and_1_out, decoder_1_out_0, CLK);
  and and_2 (and_2_out, decoder_1_out_1, CLK);
  and and_3 (and_3_out, decoder_1_out_2, CLK);
  and and_4 (and_4_out, decoder_1_out_3, CLK);
  and and_5 (and_5_out, decoder_1_out_4, CLK);
  and and_6 (and_6_out, decoder_1_out_5, CLK);
  and and_7 (and_7_out, decoder_1_out_6, CLK);
  and and_8 (and_8_out, decoder_1_out_7, CLK);
  D_FF #(.Bits(8)) d_ff_1 (.D(D), .C(and_1_out), .Q(d_ff_1_q));  // open: nQ
  D_FF #(.Bits(8)) d_ff_2 (.D(D), .C(and_2_out), .Q(d_ff_2_q));  // open: nQ
  D_FF #(.Bits(8)) d_ff_3 (.D(D), .C(and_3_out), .Q(d_ff_3_q));  // open: nQ
  D_FF #(.Bits(8)) d_ff_4 (.D(D), .C(and_4_out), .Q(d_ff_4_q));  // open: nQ
  D_FF #(.Bits(8)) d_ff_5 (.D(D), .C(and_5_out), .Q(d_ff_5_q));  // open: nQ
  D_FF #(.Bits(8)) d_ff_6 (.D(D), .C(and_6_out), .Q(d_ff_6_q));  // open: nQ
  D_FF #(.Bits(8)) d_ff_7 (.D(D), .C(and_7_out), .Q(d_ff_7_q));  // open: nQ
  D_FF #(.Bits(8)) d_ff_8 (.D(D), .C(and_8_out), .Q(d_ff_8_q));  // open: nQ
  Comparator #(.Bits(5)) comparator_1 (.a(counter_1_out), .b(5'b10000), .eq(CS));  // open: gt, lt
  Counter #(.Bits(4)) counter_2 (.en(1'b1), .C(CS), .clr(comparator_2_eq), .out(counter_2_out));  // open: ovf
  Multiplexer #(.Selector_Bits(4), .Bits(8)) multiplexer_1 (
    .sel(counter_2_out), .in_0({8{1'b0}}), .in_1(d_ff_1_q), .in_2(d_ff_2_q), .in_3(d_ff_3_q),
    .in_4(d_ff_4_q), .in_5(d_ff_5_q), .in_6(d_ff_6_q), .in_7(d_ff_7_q), .in_8(d_ff_8_q), .in_9({8{1'b0}}),
    .in_10({4'b0000, Brilho}), .in_11(8'h7), .in_12(8'h1), .in_13({8{1'b0}}), .in_14({8{1'b0}}),
    .in_15({8{1'b0}}), .out(multiplexer_1_out));
  Comparator #(.Bits(4)) comparator_2 (.a(counter_2_out), .b(4'b1100), .eq(comparator_2_eq));  // open: gt, lt
  not not_1 (CLKout, CLK);
  RegParSer16 regparser16_1 (.Ld(CS), .Clk(CLK), .Data({4'b0000, counter_2_out, multiplexer_1_out}), .Q(DO));

  // Notes on the sheet:
  //   CLK: Hz: 1000
endmodule
