// Digital circuit Driver_MAX7219.dig as structural Verilog
module Driver_MAX7219 (
  input  [3:0] Dig0,
  input  [3:0] Dig1,
  input  [3:0] Dig2,
  input  [3:0] Dig3,
  input  [3:0] Dig4,
  input  [3:0] Dig5,
  input  [3:0] Dig6,
  input  [3:0] Dig7,
  input  [3:0] Brilho,
  input  CLK,
  output DO,
  output CS,
  output CLKout
);

  wire comparator_2_eq;
  wire [3:0] counter_2_out;
  wire [4:0] counter_1_out;
  wire [7:0] multiplexer_1_out;

  Counter #(.Bits(5)) counter_1 (.en(1'b1), .C(CLK), .clr(CS), .out(counter_1_out));  // open: ovf
  Comparator #(.Bits(5)) comparator_1 (.a(counter_1_out), .b(5'b10000), .eq(CS));  // open: gt, lt
  Counter #(.Bits(4)) counter_2 (.en(1'b1), .C(CS), .clr(comparator_2_eq), .out(counter_2_out));  // open: ovf
  Multiplexer #(.Selector_Bits(4), .Bits(8)) multiplexer_1 (
    .sel(counter_2_out), .in_0({8{1'b0}}), .in_1({4'b0000, Dig0}), .in_2({4'b0000, Dig1}),
    .in_3({4'b0000, Dig2}), .in_4({4'b0000, Dig3}), .in_5({4'b0000, Dig4}), .in_6({4'b0000, Dig5}),
    .in_7({4'b0000, Dig6}), .in_8({4'b0000, Dig7}), .in_9({8{1'b1}}), .in_10({4'b0000, Brilho}),
    .in_11(8'h7), .in_12(8'h1), .in_13({8{1'b0}}), .in_14({8{1'b0}}), .in_15({8{1'b0}}),
    .out(multiplexer_1_out));
  Comparator #(.Bits(4)) comparator_2 (.a(counter_2_out), .b(4'b1100), .eq(comparator_2_eq));  // open: gt, lt
  not not_1 (CLKout, CLK);
  RegParSer16 regparser16_1 (.Ld(CS), .Clk(CLK), .Data({4'b0000, counter_2_out, multiplexer_1_out}), .Q(DO));

  // Notes on the sheet:
  //   CLK: Hz: 1000
endmodule
