// Digital circuit FonteGLCD.dig as structural Verilog
module FonteGLCD (
  input  clk
);

  wire and_1_out, and_2_out, and_3_out, button_1_out, not_1_out, rs_ff_as_1_q;
  wire [2:0] counter_1_out_2;
  wire [7:0] counter_1_out, rom_1_d;

  Button button_1 (.out(button_1_out));
  not not_1 (not_1_out, button_1_out);
  and and_1 (and_1_out, not_1_out, and_3_out);
  RS_FF_AS rs_ff_as_1 (.S(button_1_out), .R(and_1_out), .Q(rs_ff_as_1_q));  // open: nQ
  Seven_Seg_Hex seven_seg_hex_1 (.d({1'b0, counter_1_out_2}), .dp(1'b0));
  and and_2 (and_2_out, clk, rs_ff_as_1_q);
  Counter #(.Bits(11)) counter_1 (
    .en(1'b1), .C(and_2_out), .clr(1'b0), .out({counter_1_out_2, counter_1_out}));  // open: ovf
  Seven_Seg_Hex seven_seg_hex_2 (.d(counter_1_out[7:4]), .dp(1'b0));
  Seven_Seg_Hex seven_seg_hex_3 (.d(counter_1_out[3:0]), .dp(1'b0));
  ROM #(.AddrBits(11), .Bits(8)) rom_1 (.A({counter_1_out_2, counter_1_out}), .sel(1'b1), .D(rom_1_d));
  and and_3 (and_3_out, counter_1_out[0], counter_1_out[1], counter_1_out[2]);
  LedMatrix #(.ledPersistence("true")) ledmatrix_1 (.rows(rom_1_d), .column(counter_1_out[2:0]));

  // Notes on the sheet:
  //   clk: Hz: 50
  //   contents of rom_1 (hex, n*v repeats v):
  //   8*0,7e,81,a5,81,9d,b9,81,7e,7e,ff,db,ff,e3,c7,ff,7e,6c,fe,fe,fe
  //   ,7c,38,10,0,10,38,7c,fe,7c,38,10,0,38,7c,38,fe,fe,10,10,7c,0,18
  //   ,3c,7e,ff,7e,18,7e,0,0,18,3c,3c,18,0,0,ff,ff,e7,c3,c3,e7,ff,ff
  //   ,0,3c,66,42,42,66,3c,0,ff,c3,99,bd,bd,99,c3,ff,f,7,f,7d,cc,cc,cc
  //   ,78,3c,66,66,66,3c,18,7e,18,3f,33,3f,30,30,70,f0,e0,7f,63,7f,63,63
  //   ,67,e6,c0,99,5a,3c,e7,e7,3c,5a,99,80,e0,f8,fe,f8,e0,80,0,2,e,3e
  //   ,fe,3e,e,2,0,18,3c,7e,18,18,7e,3c,18,5*66,0,66,0,7f,db,db,7b,1b,1b,1b
  //   ,0,3f,60,7c,66,66,3e,6,fc,4*0,7e,7e,7e,0,18,3c,7e,18,7e,3c,18
  //   ,ff,18,3c,7e,4*18,0,4*18,7e,3c,18,0,0,18,c,fe,c,18,0,0,0,30,60
  //   ,fe,60,30,4*0,c0,c0,c0,fe,0,0,0,24,66,ff,66,24,0,0,0,18,3c,7e
  //   ,ff,ff,0,0,0,ff,ff,7e,3c,18,10*0,5*18,0,18,0,6c,6c,6c,5*0,6c,6c
  //   ,fe,6c,fe,6c,6c,0,18,7e,c0,7c,6,fc,18,0,0,c6,cc,18,30,66,c6,0
  //   ,38,6c,38,76,dc,cc,76,0,30,30,60,5*0,c,18,30,30,30,18,c,0,30,18
  //   ,c,c,c,18,30,0,0,66,3c,ff,3c,66,0,0,0,18,18,7e,18,18,7*0,18,18
  //   ,30,0,0,0,7e,9*0,18,18,0,6,c,18,30,60,c0,80,0,7c,ce,de,f6,e6,c6
  //   ,7c,0,18,38,4*18,7e,0,7c,c6,6,7c,c0,c0,fe,0,fc,6,6,3c,6,6,fc,0
  //   ,c,cc,cc,cc,fe,c,c,0,fe,c0,fc,6,6,c6,7c,0,7c,c0,c0,fc,c6,c6,7c
  //   ,0,fe,6,6,c,18,30,30,0,7c,c6,c6,7c,c6,c6,7c,0,7c,c6,c6,7e,6,6
  //   ,7c,0,0,18,18,0,0,18,18,0,0,18,18,0,0,18,18,30,c,18,30,60,30,18
  //   ,c,0,0,0,7e,0,7e,0,0,0,30,18,c,6,c,18,30,0,3c,66,c,18,18,0,18
  //   ,0,7c,c6,de,de,de,c0,7e,0,38,6c,c6,c6,fe,c6,c6,0,fc,c6,c6,fc,c6,c6
  //   ,fc,0,7c,c6,c0,c0,c0,c6,7c,0,f8,cc,c6,c6,c6,cc,f8,0,fe,c0,c0,f8
  //   ,c0,c0,fe,0,fe,c0,c0,f8,c0,c0,c0,0,7c,c6,c0,c0,ce,c6,7c,0,c6,c6,c6
  //   ,fe,c6,c6,c6,0,7e,5*18,7e,0,5*6,c6,7c,0,c6,cc,d8,f0,d8,cc,c6,0
  //   ,6*c0,fe,0,c6,ee,fe,fe,d6,c6,c6,0,c6,e6,f6,de,ce,c6,c6,0,7c,5*c6
  //   ,7c,0,fc,c6,c6,fc,c0,c0,c0,0,7c,c6,c6,c6,d6,de,7c,6,fc,c6,c6,fc
  //   ,d8,cc,c6,0,7c,c6,c0,7c,6,c6,7c,0,ff,6*18,0,6*c6,fe,0,5*c6,7c
  //   ,38,0,4*c6,d6,fe,6c,0,c6,c6,6c,38,6c,c6,c6,0,c6,c6,c6,7c,18,30
  //   ,e0,0,fe,6,c,18,30,60,fe,0,3c,5*30,3c,0,c0,60,30,18,c,6,2,0,3c
  //   ,5*c,3c,0,10,38,6c,c6,11*0,ff,18,18,c,7*0,7c,6,7e,c6,7e,0,c0,c0,c0
  //   ,fc,c6,c6,fc,0,0,0,7c,c6,c0,c6,7c,0,6,6,6,7e,c6,c6,7e,0,0,0,7c
  //   ,c6,fe,c0,7c,0,1c,36,30,78,30,30,78,0,0,0,7e,c6,c6,7e,6,fc,c0,c0
  //   ,fc,4*c6,0,18,0,38,18,18,18,3c,0,6,0,4*6,c6,7c,c0,c0,cc,d8,f8
  //   ,cc,c6,0,38,5*18,3c,0,0,0,cc,fe,fe,d6,d6,0,0,0,fc,4*c6,0,0,0,7c
  //   ,c6,c6,c6,7c,0,0,0,fc,c6,c6,fc,c0,c0,0,0,7e,c6,c6,7e,6,6,0,0,fc
  //   ,c6,c0,c0,c0,0,0,0,7e,c0,7c,6,fc,0,18,18,7e,18,18,18,e,0,0,0,4*c6
  //   ,7e,0,0,0,c6,c6,c6,7c,38,0,0,0,c6,c6,d6,fe,6c,0,0,0,c6,6c,38,6c
  //   ,c6,0,0,0,c6,c6,c6,7e,6,fc,0,0,fe,c,38,60,fe,0,e,18,18,70,18,18
  //   ,e,0,18,18,18,0,18,18,18,0,70,18,18,e,18,18,70,0,76,dc,7*0,10
  //   ,38,6c,c6,c6,fe,0,7c,c6,c0,c0,c0,d6,7c,30,c6,0,4*c6,7e,0,e,0,7c
  //   ,c6,fe,c0,7c,0,7e,81,3c,6,7e,c6,7e,0,66,0,7c,6,7e,c6,7e,0,e0,0
  //   ,7c,6,7e,c6,7e,0,18,18,7c,6,7e,c6,7e,0,0,0,7c,c6,c0,d6,7c,30,7e
  //   ,81,7c,c6,fe,c0,7c,0,66,0,7c,c6,fe,c0,7c,0,e0,0,7c,c6,fe,c0,7c
  //   ,0,66,0,38,18,18,18,3c,0,7c,82,38,18,18,18,3c,0,70,0,38,18,18,18
  //   ,3c,0,c6,10,7c,c6,fe,c6,c6,0,38,38,0,7c,c6,fe,c6,0,e,0,fe,c0,f8
  //   ,c0,fe,0,0,0,7f,c,7f,cc,7f,0,3f,6c,cc,ff,cc,cc,cf,0,7c,82,7c,c6,c6,c6
  //   ,7c,0,66,0,7c,c6,c6,c6,7c,0,e0,0,7c,c6,c6,c6,7c,0,7c,82,0,c6,c6,c6
  //   ,7e,0,e0,0,4*c6,7e,0,66,0,66,66,66,3e,6,7c,c6,7c,4*c6,7c,0,c6
  //   ,0,4*c6,fe,0,18,18,7e,d8,d8,d8,7e,18,38,6c,60,f0,60,66,fc,0,66,66
  //   ,3c,18,7e,18,7e,18,f8,cc,cc,fa,c6,cf,c6,c3,e,1b,18,3c,18,18,d8
  //   ,70,e,0,7c,6,7e,c6,7e,0,1c,0,38,18,18,18,3c,0,e,0,7c,c6,c6,c6
  //   ,7c,0,e,0,4*c6,7e,0,0,fe,0,fc,c6,c6,c6,0,fe,0,c6,e6,f6,de,ce,0
  //   ,3c,6c,6c,3e,0,7e,0,0,3c,66,66,3c,0,7e,0,0,18,0,18,18,30,66,3c
  //   ,4*0,fc,c0,c0,5*0,fc,c,c,0,0,c6,cc,d8,3f,63,cf,8c,f,c3,c6,cc,db
  //   ,37,6d,cf,3,18,0,5*18,0,0,33,66,cc,66,33,0,0,0,cc,66,33,66,cc
  //   ,0,0,22,88,22,88,22,88,22,88,55,aa,55,aa,55,aa,55,aa,dd,77,dd
  //   ,77,dd,77,dd,77,12*18,f8,5*18,f8,18,f8,18,18,18,4*36,f6,36,36,36
  //   ,4*0,fe,36,36,36,0,0,f8,18,f8,18,18,18,36,36,f6,6,f6,11*36,0,0
  //   ,fe,6,f6,5*36,f6,6,fe,0,0,0,4*36,fe,0,0,0,18,18,f8,18,f8,7*0,f8
  //   ,7*18,1f,0,0,0,4*18,ff,7*0,ff,7*18,1f,18,18,18,4*0,ff,0,0,0,4*18
  //   ,ff,5*18,1f,18,1f,18,18,18,4*36,37,5*36,37,30,3f,5*0,3f,30,37
  //   ,5*36,f7,0,ff,5*0,ff,0,f7,5*36,37,30,37,36,36,36,0,0,ff,0,ff,0,0,0
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endmodule
