// Digital circuit JKen.dig as structural Verilog
module JKen (
  input  en,
  input  J,
  input  C,
  input  K,
  output Q,
  output nQ
);

  wire and_1_out, and_2_out;

  and and_1 (and_1_out, J, en);
  and and_2 (and_2_out, en, K);
  JK_FF #(.Default(1)) jk_ff_1 (.J(and_1_out), .C(C), .K(and_2_out), .Q(Q), .nQ(nQ));
endmodule
