// Digital circuit LeTecMat.dig as structural Verilog
module LeTecMat (
  input  clk,
  output C
);

  wire _0_a, _0_b, _1_b, _2_b, _3_b, _4_a, _8_a, _10_a, _10_b, _11_b, _12_b, _13_b, _14_a, _18_a, C_2_a, C_a,
       d_ff_1_q, jk_ff_1_q, jk_ff_2_q, jk_ff_as_1_q, letecmat4x4_1_kp, letecmat4x4_1_q0, letecmat4x4_1_q1,
       letecmat4x4_1_q2, letecmat4x4_1_q3, not_1_out, not_2_out, or_1_out, or_2_out, or_3_out;
  wire [3:0] d_ff_2_q, d_ff_6_q;

  // Probe L1 on _0_a
  // Probe L2 on _4_a
  // Probe L3 on _8_a
  // Probe L4 on C_a
  Switch _0 (.A(_0_a), .B(_0_b));
  Switch _4 (.A(_4_a), .B(_0_b));
  Switch _8 (.A(_8_a), .B(_0_b));
  Switch u_C (.A(C_a), .B(_0_b));
  Switch _10 (.A(_10_a), .B(_10_b));
  Switch _14 (.A(_14_a), .B(_10_b));
  Switch _18 (.A(_18_a), .B(_10_b));
  Switch C_2 (.A(C_2_a), .B(_10_b));
  Switch _1 (.A(_0_a), .B(_1_b));
  Switch _5 (.A(_4_a), .B(_1_b));
  Switch _9 (.A(_8_a), .B(_1_b));
  Switch D (.A(C_a), .B(_1_b));
  PullDown pulldown_1 (.out(_0_b));
  Switch _11 (.A(_10_a), .B(_11_b));
  Switch _15 (.A(_14_a), .B(_11_b));
  Switch _19 (.A(_18_a), .B(_11_b));
  Switch D_2 (.A(C_2_a), .B(_11_b));
  PullDown pulldown_2 (.out(_10_b));
  Switch _2 (.A(_0_a), .B(_2_b));
  Switch _6 (.A(_4_a), .B(_2_b));
  Switch A (.A(_8_a), .B(_2_b));
  Switch E (.A(C_a), .B(_2_b));
  PullDown pulldown_3 (.out(_1_b));
  Switch _12 (.A(_10_a), .B(_12_b));
  Switch _16 (.A(_14_a), .B(_12_b));
  Switch A_2 (.A(_18_a), .B(_12_b));
  Switch E_2 (.A(C_2_a), .B(_12_b));
  PullDown pulldown_4 (.out(_11_b));
  Switch _3 (.A(_0_a), .B(_3_b));
  Switch _7 (.A(_4_a), .B(_3_b));
  Switch B (.A(_8_a), .B(_3_b));
  Switch F (.A(C_a), .B(_3_b));
  PullDown pulldown_5 (.out(_2_b));
  Switch _13 (.A(_10_a), .B(_13_b));
  Switch _17 (.A(_14_a), .B(_13_b));
  Switch B_2 (.A(_18_a), .B(_13_b));
  Switch F_2 (.A(C_2_a), .B(_13_b));
  PullDown pulldown_6 (.out(_12_b));
  PullDown pulldown_7 (.out(_3_b));
  PullDown pulldown_8 (.out(_13_b));
  or or_1 (or_1_out, _1_b, _3_b);
  or or_2 (or_2_out, _2_b, _3_b);
  or or_3 (or_3_out, _3_b, _2_b, _1_b, _0_b);
  JK_FF jk_ff_1 (.J(1'b1), .C(clk), .K(1'b1), .Q(jk_ff_1_q));  // open: nQ
  and and_1 (_0_a, not_2_out, not_1_out);
  and and_2 (_4_a, not_2_out, jk_ff_1_q);
  and and_3 (_8_a, jk_ff_2_q, not_1_out);
  and and_4 (C_a, jk_ff_2_q, jk_ff_1_q);
  LeTecMat4x4 letecmat4x4_1 (
    .clk(clk), .L0(_10_a), .L1(_14_a), .L2(_18_a), .L3(C_2_a), .C0(_10_b), .C1(_11_b), .C2(_12_b),
    .C3(_13_b), .Q0(letecmat4x4_1_q0), .Q1(letecmat4x4_1_q1), .Q2(letecmat4x4_1_q2), .Q3(letecmat4x4_1_q3),
    .Kp(letecmat4x4_1_kp));
  not not_1 (not_1_out, jk_ff_1_q);
  JK_FF_AS jk_ff_as_1 (.Set(or_3_out), .J(1'b0), .C(~C_a), .K(1'b1), .Clr(1'b0), .Q(jk_ff_as_1_q));  // open: nQ
  JK_FF jk_ff_2 (.J(jk_ff_1_q), .C(clk), .K(jk_ff_1_q), .Q(jk_ff_2_q));  // open: nQ
  not not_2 (not_2_out, jk_ff_2_q);
  D_FF d_ff_1 (.D(jk_ff_as_1_q), .C(~C_a), .Q(d_ff_1_q));  // open: nQ
  D_FF d_ff_2 (.D(letecmat4x4_1_q0), .C(letecmat4x4_1_kp), .Q(d_ff_2_q[0]));  // open: nQ
  D_FF d_ff_3 (.D(letecmat4x4_1_q1), .C(letecmat4x4_1_kp), .Q(d_ff_2_q[1]));  // open: nQ
  D_FF d_ff_4 (.D(letecmat4x4_1_q2), .C(letecmat4x4_1_kp), .Q(d_ff_2_q[2]));  // open: nQ
  D_FF d_ff_5 (.D(letecmat4x4_1_q3), .C(letecmat4x4_1_kp), .Q(d_ff_2_q[3]));  // open: nQ
  or or_4 (C, jk_ff_as_1_q, d_ff_1_q);
  Seven_Seg_Hex seven_seg_hex_1 (.d(d_ff_2_q), .dp(1'b0));
  D_FF d_ff_6 (.D(or_1_out), .C(C), .Q(d_ff_6_q[0]));  // open: nQ
  D_FF d_ff_7 (.D(or_2_out), .C(C), .Q(d_ff_6_q[1]));  // open: nQ
  D_FF d_ff_8 (.D(jk_ff_1_q), .C(C), .Q(d_ff_6_q[2]));  // open: nQ
  D_FF d_ff_9 (.D(jk_ff_2_q), .C(C), .Q(d_ff_6_q[3]));  // open: nQ
  Seven_Seg_Hex seven_seg_hex_2 (.d(d_ff_6_q), .dp(1'b0));

  // Notes on the sheet:
  //   clk: Hz: 3
endmodule
