// Digital circuit LeTecMat4x4.dig as structural Verilog
module LeTecMat4x4 (
  input  clk,
  input  C0,
  input  C1,
  input  C2,
  input  C3,
  output Q0,
  output Q1,
  output Q2,
  output Q3,
  output L0,
  output L1,
  output L2,
  output L3,
  output Kp
);

  wire d_ff_1_q, d_ff_2_q, d_ff_3_q, d_ff_4_q, d_ff_5_q, d_ff_6_q, d_ff_7_q, d_ff_8_q, d_ff_as_1_nq,
       d_ff_as_1_q, d_ff_as_2_nq, d_ff_as_2_q, d_ff_as_3_nq, d_ff_as_3_q, jk_ff_1_q, jk_ff_2_q, not_1_out,
       not_2_out, or_1_out, or_2_out, or_3_out, or_4_out;
  wire [3:0] d_ff_9_q;

  or or_1 (or_1_out, C1, C3);
  or or_2 (or_2_out, C2, C3);
  or or_3 (or_3_out, C3, C2, C1, C0);
  D_FF d_ff_1 (.D(or_3_out), .C(clk), .Q(d_ff_1_q));  // open: nQ
  JK_FF jk_ff_1 (.J(1'b1), .C(clk), .K(1'b1), .Q(jk_ff_1_q));  // open: nQ
  and and_1 (L0, not_2_out, not_1_out);
  and and_2 (L1, not_2_out, jk_ff_1_q);
  and and_3 (L2, jk_ff_2_q, not_1_out);
  and and_4 (L3, jk_ff_2_q, jk_ff_1_q);
  D_FF d_ff_2 (.D(d_ff_1_q), .C(clk), .Q(d_ff_2_q));  // open: nQ
  not not_1 (not_1_out, jk_ff_1_q);
  D_FF d_ff_3 (.D(d_ff_2_q), .C(clk), .Q(d_ff_3_q));  // open: nQ
  JK_FF jk_ff_2 (.J(jk_ff_1_q), .C(clk), .K(jk_ff_1_q), .Q(jk_ff_2_q));  // open: nQ
  not not_2 (not_2_out, jk_ff_2_q);
  or or_4 (or_4_out, or_3_out, d_ff_1_q, d_ff_2_q, d_ff_3_q);
  D_FF d_ff_4 (.D(or_4_out), .C(clk), .Q(d_ff_4_q));  // open: nQ
  D_FF_AS d_ff_as_1 (.Set(Kp), .D(d_ff_as_1_nq), .C(L3), .Clr(~d_ff_4_q), .Q(d_ff_as_1_q), .nQ(d_ff_as_1_nq));
  D_FF d_ff_5 (.D(or_1_out), .C(or_3_out), .Q(d_ff_5_q));  // open: nQ
  D_FF d_ff_6 (.D(or_2_out), .C(or_3_out), .Q(d_ff_6_q));  // open: nQ
  D_FF d_ff_7 (.D(jk_ff_1_q), .C(or_3_out), .Q(d_ff_7_q));  // open: nQ
  D_FF d_ff_8 (.D(jk_ff_2_q), .C(or_3_out), .Q(d_ff_8_q));  // open: nQ
  D_FF_AS d_ff_as_2 (
    .Set(1'b0), .D(d_ff_as_2_nq), .C(d_ff_as_1_nq), .Clr(~d_ff_4_q), .Q(d_ff_as_2_q), .nQ(d_ff_as_2_nq));
  D_FF_AS d_ff_as_3 (
    .Set(1'b0), .D(d_ff_as_3_nq), .C(d_ff_as_2_nq), .Clr(~d_ff_4_q), .Q(d_ff_as_3_q), .nQ(d_ff_as_3_nq));
  and and_5 (Kp, d_ff_as_1_q, d_ff_as_2_q, d_ff_as_3_q);
  D_FF d_ff_9 (.D(d_ff_5_q), .C(Kp), .Q(d_ff_9_q[0]));  // open: nQ
  D_FF d_ff_10 (.D(d_ff_6_q), .C(Kp), .Q(d_ff_9_q[1]));  // open: nQ
  D_FF d_ff_11 (.D(d_ff_7_q), .C(Kp), .Q(d_ff_9_q[2]));  // open: nQ
  D_FF d_ff_12 (.D(d_ff_8_q), .C(Kp), .Q(d_ff_9_q[3]));  // open: nQ
  ROM #(.AddrBits(4), .Bits(4)) m (.A(d_ff_9_q), .sel(1'b1), .D({Q3, Q2, Q1, Q0}));

  // Notes on the sheet:
  //   clk: Hz: 2
  //   contents of m (hex, n*v repeats v):
  //   1,2,3,a,4,5,6,b,7,8,9,c,e,0,f,d
endmodule
