// Digital circuit LeitorADC0831.dig as structural Verilog
module LeitorADC0831 (
  input  clock_50,
  input  Din,
  output clock_out,
  output CS,
  output [7:0] AD_data
);

  wire d_ff_1_q;
  wire [3:0] counter_1_out;
  wire [7:0] regdesl8_1_q;

  Div8FF div8ff_1 (.CLK_in(clock_50), .CLK_out(clock_out));
  Counter #(.Bits(4)) counter_1 (.en(1'b1), .C(clock_out), .clr(1'b0), .out(counter_1_out));  // open: ovf
  RegDesl8 regdesl8_1 (.Clock(clock_out), .D(Din), .Q(regdesl8_1_q));
  Comparator #(.Bits(4)) comparator_1 (.a(counter_1_out), .b(4'b1001), .gt(CS));  // open: eq, lt
  D_FF d_ff_1 (.D(CS), .C(clock_50), .Q(d_ff_1_q));  // open: nQ
  Register #(.Bits(8)) register_1 (.D(regdesl8_1_q), .C(d_ff_1_q), .en(1'b1), .Q(AD_data));
endmodule
