// Digital circuit MultLim16.dig as structural Verilog
module MultLim16 (
  input  [15:0] A,
  input  [15:0] B,
  output [15:0] Y
);

  wire comparator_1_lt, comparator_2_gt;
  wire [31:0] mul_1_mul, multiplexer_1_out;
  wire [31:16] multiplexer_2_out;

  Mul #(.Signed("true"), .Bits(16)) mul_1 (.a(A), .b(B), .mul(mul_1_mul));
  Comparator #(.Signed("true"), .Bits(32)) comparator_1 (
    .a(mul_1_mul), .b(32'hffff8000), .lt(comparator_1_lt));  // open: gt, eq
  Multiplexer #(.Bits(32)) multiplexer_1 (
    .sel(comparator_1_lt), .in_0(mul_1_mul), .in_1(32'hffff8000), .out(multiplexer_1_out));
  Comparator #(.Signed("true"), .Bits(32)) comparator_2 (
    .a(multiplexer_1_out), .b(32'h7fff), .gt(comparator_2_gt));  // open: eq, lt
  Multiplexer #(.Bits(32)) multiplexer_2 (
    .sel(comparator_2_gt), .in_0(multiplexer_1_out), .in_1(32'h7fff), .out({multiplexer_2_out, Y}));
endmodule

/* Test case:
A B Y
10 34 340
# -10 34 -340
0xFFF6 34 0xFEAC
# 10 -34 -340
10 0xFFDE 0xFEAC
3276 10 32760
3276 11 32767
# 3276 -10 -32760
3276 0xFFF6 0x8008
#3276 -11 -32768
3276 0xFFF5 0x8000
*/
