// Digital circuit PI.dig as structural Verilog
module PI (
  input  [7:0] SP,
  input  [7:0] PV,
  input  [15:0] KP,
  input  CLK_I,
  input  [24:0] ClkDiv,
  output [15:0] MV,
  output ClkPI
);

  wire comparator_1_gt, d_ff_1_q;
  wire [7:0] Er, multiplexer_1_out;
  wire [15:0] I, multiplexer_2_out, P, signed8to16_1_out_16, somalimiteu16_2_y;

  Comparator #(.Bits(8)) comparator_1 (.a(PV), .b(8'h7f), .gt(comparator_1_gt));  // open: eq, lt
  Divisor divisor_1 (.ClkIn(CLK_I), .div(ClkDiv), .ClkOut(ClkPI));
  Multiplexer #(.Bits(8)) multiplexer_1 (.sel(comparator_1_gt), .in_0(PV), .in_1(8'h7f), .out(multiplexer_1_out));
  Sub #(.Bits(8)) sub_1 (.a(SP), .b(multiplexer_1_out), .c_i(1'b0), .s(Er));  // open: c_o
  D_FF d_ff_1 (.D(1'b1), .C(ClkPI), .Q(d_ff_1_q));  // open: nQ
  Signed8to16 signed8to16_1 (.IN_8(Er), .OUT_16(signed8to16_1_out_16));
  Multiplexer #(.Bits(16)) multiplexer_2 (
    .sel(d_ff_1_q), .in_0(16'h8000), .in_1(somalimiteu16_2_y), .out(multiplexer_2_out));
  Register #(.Bits(16)) register_1 (.D(multiplexer_2_out), .C(ClkPI), .en(1'b1), .Q(I));
  MultLim16 multlim16_1 (.A(KP), .B(signed8to16_1_out_16), .Y(P));
  SomaLimiteU16 somalimiteu16_1 (.A(P), .B(I), .Y(MV));
  SomaLimiteU16 somalimiteu16_2 (.A(signed8to16_1_out_16), .B(I), .Y(somalimiteu16_2_y));
  // Probe on Er
  // Probe on P
  // Probe on I

  // Notes on the sheet:
  //   CLK_I: Hz: 5
  //   ClkDiv: default 10
endmodule
