// Digital circuit PI8.dig as structural Verilog
module PI8 (
  input  [7:0] SP,
  input  [7:0] PV,
  input  [7:0] KP,
  input  CLK_I,
  output [7:0] MV
);

  wire comparator_1_lt, comparator_2_gt;
  wire [7:0] add_2_s, Er, I, multiplexer_1_out, multiplexer_2_out;

  Sub #(.Bits(8)) sub_1 (.a(SP), .b(PV), .c_i(1'b0), .s(Er));  // open: c_o
  Register #(.Bits(8)) register_1 (.D(multiplexer_1_out), .C(CLK_I), .en(1'b1), .Q(I));
  Multiplexer #(.Bits(8)) multiplexer_1 (
    .sel(comparator_1_lt), .in_0(multiplexer_2_out), .in_1(8'h88), .out(multiplexer_1_out));
  Comparator #(.Signed("true"), .Bits(8)) comparator_1 (.lt(comparator_1_lt));  // open: a, b, gt, eq
  Multiplexer #(.Bits(8)) multiplexer_2 (.sel(comparator_2_gt), .in_0(add_2_s), .in_1(8'h78), .out(multiplexer_2_out));
  Add #(.Bits(8)) add_1 (.a(Er), .b(I), .c_i(1'b0), .s(MV));  // open: c_o
  Add #(.Bits(8)) add_2 (.a(Er), .b(I), .c_i(1'b0), .s(add_2_s));  // open: c_o
  Comparator #(.Signed("true"), .Bits(8)) comparator_2 (.gt(comparator_2_gt));  // open: a, b, eq, lt
  // Probe on Er
  // Probe on Er
  // Probe on I

  // Other names for the same wires on the sheet: P[7:0] = Er

  // Notes on the sheet:
  //   CLK_I: Hz: 100
endmodule
