// Digital circuit PWM.dig as structural Verilog
module PWM (
  input  CLK_50,
  input  Data_in,
  output PWM_out,
  output CLK_out,
  output CS,
  output a,
  output b,
  output c,
  output d,
  output e,
  output f,
  output g,
  output NPWM_out,
  output S_out
);

  wire div5ff_1_clk_out, divisor_1_clkout, not_1_out, txserial_1_buzy;
  wire [7:0] cont8_1_q, leitoradc0831_1_ad_data;

  Div5FF div5ff_1 (.CLK_in(CLK_50), .CLK_out(div5ff_1_clk_out));
  Divisor divisor_1 (.ClkIn(CLK_50), .div(25'h516), .ClkOut(divisor_1_clkout));
  LeitorADC0831 leitoradc0831_1 (
    .clock_50(CLK_50), .Din(Data_in), .clock_out(CLK_out), .CS(CS), .AD_data(leitoradc0831_1_ad_data));
  cont8 cont8_1 (.clock(div5ff_1_clk_out), .Reset(1'b0), .Q(cont8_1_q));
  TxSerial txserial_1 (
    .Transmit(not_1_out), .Data_in(leitoradc0831_1_ad_data), .Clock(divisor_1_clkout), .S_out(S_out),
    .Buzy(txserial_1_buzy));
  not not_1 (not_1_out, txserial_1_buzy);
  Comparator #(.Bits(8)) comparator_1 (.a(cont8_1_q), .b(leitoradc0831_1_ad_data), .lt(PWM_out));  // open: gt, eq
  Driver7seg driver7seg_1 (.Din(leitoradc0831_1_ad_data[7:4]), .a(a), .b(b), .c(c), .d(d), .e(e), .f(f), .g(g));
  not not_2 (NPWM_out, PWM_out);

  // Notes on the sheet:
  //   CLK_50: Hz: 50
  //   19200 bps
endmodule
