// Digital circuit Reg4Reset.dig as structural Verilog
module Reg4Reset (
  input  X_2,
  input  X_1,
  input  X_0,
  input  X_3,
  input  CLK,
  input  RST,
  output Y_2,
  output Y_1,
  output Y_0,
  output Y_3
);

  D_FF_AS d_ff_as_1 (.Set(1'b0), .D(X_0), .C(CLK), .Clr(RST), .Q(Y_0));  // open: nQ
  D_FF_AS d_ff_as_2 (.Set(1'b0), .D(X_1), .C(CLK), .Clr(RST), .Q(Y_1));  // open: nQ
  D_FF_AS d_ff_as_3 (.Set(1'b0), .D(X_2), .C(CLK), .Clr(RST), .Q(Y_2));  // open: nQ
  D_FF_AS d_ff_as_4 (.Set(1'b0), .D(X_3), .C(CLK), .Clr(RST), .Q(Y_3));  // open: nQ
endmodule
