// Digital circuit RegDesl8LSB.dig as structural Verilog
module RegDesl8LSB (
  input  Clock,
  input  D,
  output [7:0] Q
);

  D_FF d_ff_1 (.D(D), .C(Clock), .Q(Q[7]));  // open: nQ
  D_FF d_ff_2 (.D(Q[7]), .C(Clock), .Q(Q[6]));  // open: nQ
  D_FF d_ff_3 (.D(Q[6]), .C(Clock), .Q(Q[5]));  // open: nQ
  D_FF d_ff_4 (.D(Q[5]), .C(Clock), .Q(Q[4]));  // open: nQ
  D_FF d_ff_5 (.D(Q[4]), .C(Clock), .Q(Q[3]));  // open: nQ
  D_FF d_ff_6 (.D(Q[3]), .C(Clock), .Q(Q[2]));  // open: nQ
  D_FF d_ff_7 (.D(Q[2]), .C(Clock), .Q(Q[1]));  // open: nQ
  D_FF d_ff_8 (.D(Q[1]), .C(Clock), .Q(Q[0]));  // open: nQ
endmodule
