// Digital circuit RegParSer16.dig as structural Verilog
module RegParSer16 (
  input  Ld,
  input  Clk,
  input  [15:0] Data,
  output Q
);

  wire and_1_out, and_2_out, and_3_out, and_4_out, and_5_out, and_6_out, and_7_out, and_8_out, and_9_out,
       and_10_out, and_11_out, and_12_out, and_13_out, and_14_out, and_15_out, and_16_out, and_17_out,
       and_18_out, and_19_out, and_20_out, and_21_out, and_22_out, and_23_out, and_24_out, and_25_out,
       and_26_out, and_27_out, and_28_out, and_29_out, and_30_out, and_31_out, d_ff_1_q, d_ff_2_q, d_ff_3_q,
       d_ff_4_q, d_ff_5_q, d_ff_6_q, d_ff_7_q, d_ff_8_q, d_ff_9_q, d_ff_10_q, d_ff_11_q, d_ff_12_q,
       d_ff_13_q, d_ff_14_q, d_ff_15_q, not_1_out, not_2_out, or_1_out, or_2_out, or_3_out, or_4_out,
       or_5_out, or_6_out, or_7_out, or_8_out, or_9_out, or_10_out, or_11_out, or_12_out, or_13_out,
       or_14_out, or_15_out;

  not not_1 (not_1_out, Clk);
  and and_1 (and_1_out, Data[0], Ld);
  D_FF d_ff_1 (.D(and_1_out), .C(not_1_out), .Q(d_ff_1_q));  // open: nQ
  not not_2 (not_2_out, Ld);
  and and_2 (and_2_out, Data[1], Ld);
  and and_3 (and_3_out, d_ff_1_q, not_2_out);
  or or_1 (or_1_out, and_2_out, and_3_out);
  D_FF d_ff_2 (.D(or_1_out), .C(not_1_out), .Q(d_ff_2_q));  // open: nQ
  and and_4 (and_4_out, Data[2], Ld);
  and and_5 (and_5_out, d_ff_2_q, not_2_out);
  or or_2 (or_2_out, and_4_out, and_5_out);
  D_FF d_ff_3 (.D(or_2_out), .C(not_1_out), .Q(d_ff_3_q));  // open: nQ
  and and_6 (and_6_out, Data[3], Ld);
  and and_7 (and_7_out, d_ff_3_q, not_2_out);
  or or_3 (or_3_out, and_6_out, and_7_out);
  D_FF d_ff_4 (.D(or_3_out), .C(not_1_out), .Q(d_ff_4_q));  // open: nQ
  and and_8 (and_8_out, Data[4], Ld);
  and and_9 (and_9_out, d_ff_4_q, not_2_out);
  or or_4 (or_4_out, and_8_out, and_9_out);
  D_FF d_ff_5 (.D(or_4_out), .C(not_1_out), .Q(d_ff_5_q));  // open: nQ
  and and_10 (and_10_out, Data[5], Ld);
  and and_11 (and_11_out, d_ff_5_q, not_2_out);
  or or_5 (or_5_out, and_10_out, and_11_out);
  D_FF d_ff_6 (.D(or_5_out), .C(not_1_out), .Q(d_ff_6_q));  // open: nQ
  and and_12 (and_12_out, Data[6], Ld);
  and and_13 (and_13_out, d_ff_6_q, not_2_out);
  or or_6 (or_6_out, and_12_out, and_13_out);
  D_FF d_ff_7 (.D(or_6_out), .C(not_1_out), .Q(d_ff_7_q));  // open: nQ
  and and_14 (and_14_out, Data[7], Ld);
  and and_15 (and_15_out, d_ff_7_q, not_2_out);
  or or_7 (or_7_out, and_14_out, and_15_out);
  D_FF d_ff_8 (.D(or_7_out), .C(not_1_out), .Q(d_ff_8_q));  // open: nQ
  and and_16 (and_16_out, Data[8], Ld);
  and and_17 (and_17_out, d_ff_8_q, not_2_out);
  or or_8 (or_8_out, and_16_out, and_17_out);
  D_FF d_ff_9 (.D(or_8_out), .C(not_1_out), .Q(d_ff_9_q));  // open: nQ
  and and_18 (and_18_out, Data[9], Ld);
  and and_19 (and_19_out, d_ff_9_q, not_2_out);
  or or_9 (or_9_out, and_18_out, and_19_out);
  D_FF d_ff_10 (.D(or_9_out), .C(not_1_out), .Q(d_ff_10_q));  // open: nQ
  and and_20 (and_20_out, Data[10], Ld);
  and and_21 (and_21_out, d_ff_10_q, not_2_out);
  or or_10 (or_10_out, and_20_out, and_21_out);
  D_FF d_ff_11 (.D(or_10_out), .C(not_1_out), .Q(d_ff_11_q));  // open: nQ
  and and_22 (and_22_out, Data[11], Ld);
  and and_23 (and_23_out, d_ff_11_q, not_2_out);
  or or_11 (or_11_out, and_22_out, and_23_out);
  D_FF d_ff_12 (.D(or_11_out), .C(not_1_out), .Q(d_ff_12_q));  // open: nQ
  and and_24 (and_24_out, Data[12], Ld);
  and and_25 (and_25_out, d_ff_12_q, not_2_out);
  or or_12 (or_12_out, and_24_out, and_25_out);
  D_FF d_ff_13 (.D(or_12_out), .C(not_1_out), .Q(d_ff_13_q));  // open: nQ
  and and_26 (and_26_out, Data[13], Ld);
  and and_27 (and_27_out, d_ff_13_q, not_2_out);
  or or_13 (or_13_out, and_26_out, and_27_out);
  D_FF d_ff_14 (.D(or_13_out), .C(not_1_out), .Q(d_ff_14_q));  // open: nQ
  and and_28 (and_28_out, Data[14], Ld);
  and and_29 (and_29_out, d_ff_14_q, not_2_out);
  or or_14 (or_14_out, and_28_out, and_29_out);
  D_FF d_ff_15 (.D(or_14_out), .C(not_1_out), .Q(d_ff_15_q));  // open: nQ
  and and_30 (and_30_out, Data[15], Ld);
  and and_31 (and_31_out, d_ff_15_q, not_2_out);
  or or_15 (or_15_out, and_30_out, and_31_out);
  D_FF d_ff_16 (.D(or_15_out), .C(not_1_out), .Q(Q));  // open: nQ
endmodule
