// Digital circuit RxSerial.dig as structural Verilog
module RxSerial (
  input  Serial_in,
  input  Enable,
  input  Clock,
  output [7:0] Data_out,
  output [3:0] out_5
);

  wire and_1_out, and_2_out, comparator_1_eq, d_ff_as_1_q, not_1_out, not_2_out;
  wire [7:0] regdesl8lsb_1_q;

  not not_1 (not_1_out, Serial_in);
  and and_1 (and_1_out, not_1_out, Enable);
  D_FF_AS d_ff_as_1 (.Set(and_1_out), .D(1'b0), .C(1'b0), .Clr(comparator_1_eq), .Q(d_ff_as_1_q));  // open: nQ
  and and_2 (and_2_out, Clock, d_ff_as_1_q);
  not not_2 (not_2_out, d_ff_as_1_q);
  RegDesl8LSB regdesl8lsb_1 (.Clock(and_2_out), .D(Serial_in), .Q(regdesl8lsb_1_q));
  cont4 cont4_1 (.clock(and_2_out), .Reset(not_2_out), .Q(out_5));
  Register #(.Bits(8)) register_1 (.D(regdesl8lsb_1_q), .C(comparator_1_eq), .en(1'b1), .Q(Data_out));
  Comparator #(.Bits(4)) comparator_1 (.a(out_5), .b(4'b1001), .eq(comparator_1_eq));  // open: gt, lt
endmodule
