// Digital circuit Senha1.dig as structural Verilog
module Senha1 (
  input  clk
);

  wire _0_a, _0_b, _1_b, _2_b, _3_b, _4_a, _8_a, a1, a2, a3, a4, and_1_out, and_2_out, and_3_out, and_4_out,
       and_5_out, b1, b2, b3, b4, c1, c2, c3, c4, C_a, comparator_1_eq, comparator_2_eq, comparator_3_eq,
       comparator_4_eq, d1, d2, d3, d4, d_ff_as_1_q, d_ff_as_2_q, d_ff_as_3_q, d_ff_as_4_q, e1, e2, e3, e4,
       f1, f2, f3, f4, g1, g2, g3, g4, letecmat4x4_1_kp, or_1_out, or_2_out, or_3_out, or_4_out, reset;
  wire [3:0] d_ff_1_q, d_ff_2_q, d_ff_3_q, d_ff_4_q, letecmat4x4_1_q0, multiplexer_1_out;

  Switch _0 (.A(_0_a), .B(_0_b));
  Switch _4 (.A(_4_a), .B(_0_b));
  Switch _8 (.A(_8_a), .B(_0_b));
  Switch C (.A(C_a), .B(_0_b));
  Switch _1 (.A(_0_a), .B(_1_b));
  Switch _5 (.A(_4_a), .B(_1_b));
  Switch _9 (.A(_8_a), .B(_1_b));
  Switch D (.A(C_a), .B(_1_b));
  PullDown pulldown_1 (.out(_0_b));
  Switch _2 (.A(_0_a), .B(_2_b));
  Switch _6 (.A(_4_a), .B(_2_b));
  Switch A (.A(_8_a), .B(_2_b));
  Switch E (.A(C_a), .B(_2_b));
  PullDown pulldown_2 (.out(_1_b));
  Switch _3 (.A(_0_a), .B(_3_b));
  Switch _7 (.A(_4_a), .B(_3_b));
  Switch B (.A(_8_a), .B(_3_b));
  Switch F (.A(C_a), .B(_3_b));
  PullDown pulldown_3 (.out(_2_b));
  PullDown pulldown_4 (.out(_3_b));
  Button u_Reset (.out(reset));
  LeTecMat4x4 letecmat4x4_1 (
    .clk(clk), .L0(_0_a), .L1(_4_a), .L2(_8_a), .L3(C_a), .C0(_0_b), .C1(_1_b), .C2(_2_b), .C3(_3_b),
    .Q0(letecmat4x4_1_q0[0]), .Q1(letecmat4x4_1_q0[1]), .Q2(letecmat4x4_1_q0[2]), .Q3(letecmat4x4_1_q0[3]),
    .Kp(letecmat4x4_1_kp));
  D_FF_AS d_ff_as_1 (.Set(reset), .D(reset), .C(~letecmat4x4_1_kp), .Clr(1'b0), .Q(d_ff_as_1_q));  // open: nQ
  Multiplexer #(.Bits(4)) multiplexer_1 (.sel(reset), .in_0(letecmat4x4_1_q0), .in_1(4'b1111), .out(multiplexer_1_out));
  or or_1 (or_1_out, reset, and_1_out);
  and and_1 (and_1_out, letecmat4x4_1_kp, d_ff_as_1_q);
  D_FF #(.Bits(4)) d_ff_1 (.D(multiplexer_1_out), .C(or_1_out), .Q(d_ff_1_q));  // open: nQ
  D_FF_AS d_ff_as_2 (.Set(1'b0), .D(d_ff_as_1_q), .C(~letecmat4x4_1_kp), .Clr(reset), .Q(d_ff_as_2_q));  // open: nQ
  Driver7segDecimal driver7segdecimal_1 (.Din(d_ff_1_q), .a(a1), .b(b1), .c(c1), .d(d1), .e(e1), .f(f1), .g(g1));
  or or_2 (or_2_out, reset, and_2_out);
  and and_2 (and_2_out, letecmat4x4_1_kp, d_ff_as_2_q);
  Seven_Seg seven_seg_1 (.a(a1), .b(b1), .c(c1), .d(d1), .e(e1), .f(f1), .g(g1), .dp(1'b0));
  D_FF #(.Bits(4)) d_ff_2 (.D(multiplexer_1_out), .C(or_2_out), .Q(d_ff_2_q));  // open: nQ
  D_FF_AS d_ff_as_3 (.Set(1'b0), .D(d_ff_as_2_q), .C(~letecmat4x4_1_kp), .Clr(reset), .Q(d_ff_as_3_q));  // open: nQ
  Driver7segDecimal driver7segdecimal_2 (.Din(d_ff_2_q), .a(a2), .b(b2), .c(c2), .d(d2), .e(e2), .f(f2), .g(g2));
  or or_3 (or_3_out, reset, and_3_out);
  and and_3 (and_3_out, letecmat4x4_1_kp, d_ff_as_3_q);
  Seven_Seg seven_seg_2 (.a(a2), .b(b2), .c(c2), .d(d2), .e(e2), .f(f2), .g(g2), .dp(1'b0));
  D_FF #(.Bits(4)) d_ff_3 (.D(multiplexer_1_out), .C(or_3_out), .Q(d_ff_3_q));  // open: nQ
  D_FF_AS d_ff_as_4 (.Set(1'b0), .D(d_ff_as_3_q), .C(~letecmat4x4_1_kp), .Clr(reset), .Q(d_ff_as_4_q));  // open: nQ
  Driver7segDecimal driver7segdecimal_3 (.Din(d_ff_3_q), .a(a3), .b(b3), .c(c3), .d(d3), .e(e3), .f(f3), .g(g3));
  or or_4 (or_4_out, reset, and_4_out);
  and and_4 (and_4_out, letecmat4x4_1_kp, d_ff_as_4_q);
  Seven_Seg seven_seg_3 (.a(a3), .b(b3), .c(c3), .d(d3), .e(e3), .f(f3), .g(g3), .dp(1'b0));
  D_FF #(.Bits(4)) d_ff_4 (.D(multiplexer_1_out), .C(or_4_out), .Q(d_ff_4_q));  // open: nQ
  Driver7segDecimal driver7segdecimal_4 (.Din(d_ff_4_q), .a(a4), .b(b4), .c(c4), .d(d4), .e(e4), .f(f4), .g(g4));
  Comparator #(.Bits(4)) comparator_1 (.a(d_ff_4_q), .b(4'b0101), .eq(comparator_1_eq));  // open: gt, lt
  Comparator #(.Bits(4)) comparator_2 (.a(d_ff_3_q), .b(4'b0100), .eq(comparator_2_eq));  // open: gt, lt
  Comparator #(.Bits(4)) comparator_3 (.a(d_ff_2_q), .b(4'b0010), .eq(comparator_3_eq));  // open: gt, lt
  Comparator #(.Bits(4)) comparator_4 (.a(d_ff_1_q), .b(4'b1001), .eq(comparator_4_eq));  // open: gt, lt
  Seven_Seg seven_seg_4 (.a(a4), .b(b4), .c(c4), .d(d4), .e(e4), .f(f4), .g(g4), .dp(1'b0));
  and and_5 (and_5_out, comparator_1_eq, comparator_2_eq, comparator_3_eq, comparator_4_eq);
  LED led_1 (.in(and_5_out));

  // Notes on the sheet:
  //   clk: Hz: 10
endmodule
