// Digital circuit Som.dig as structural Verilog
module Som (
  input  [6:0] Vol,
  input  clk
);

  // MIDI #(.midiInstrument("Sine Wave")) midi_1: pin names not known; wires that end beside it: 7'b1100100, Vol, clk, 1'b1, clk

  // Notes on the sheet:
  //   Vol: default 127
endmodule
