// Digital circuit SomaLimiteU16.dig as structural Verilog
module SomaLimiteU16 (
  input  [15:0] A,
  input  [15:0] B,
  output [15:0] Y
);

  wire comparator_1_lt, comparator_2_gt;
  wire [16:0] add_1_s, multiplexer_1_out;
  wire [16:16] multiplexer_2_out;

  Add #(.Bits(17)) add_1 (.a({{2{A[15]}}, A[14:0]}), .b({{2{B[15]}}, B[14:0]}), .c_i(1'b0), .s(add_1_s));  // open: c_o
  Comparator #(.Signed("true"), .Bits(17)) comparator_1 (
    .a(add_1_s), .b(17'h18000), .lt(comparator_1_lt));  // open: gt, eq
  Multiplexer #(.Bits(17)) multiplexer_1 (
    .sel(comparator_1_lt), .in_0(add_1_s), .in_1(17'h18000), .out(multiplexer_1_out));
  Comparator #(.Signed("true"), .Bits(17)) comparator_2 (
    .a(multiplexer_1_out), .b(17'h7fff), .gt(comparator_2_gt));  // open: eq, lt
  Multiplexer #(.Bits(17)) multiplexer_2 (
    .sel(comparator_2_gt), .in_0(multiplexer_1_out), .in_1(17'h7fff), .out({multiplexer_2_out[16], Y}));
endmodule
