// Digital circuit TesteContador.dig as structural Verilog
module TesteContador (
  input  in_1,
  input  in_2
);

  wire contadorhexa_1_qa, contadorhexa_1_qb, contadorhexa_1_qc, contadorhexa_1_qd,
       decodificador7segmentos_1_a, decodificador7segmentos_1_b, decodificador7segmentos_1_c,
       decodificador7segmentos_1_d, decodificador7segmentos_1_e, decodificador7segmentos_1_f,
       decodificador7segmentos_1_g;

  ContadorHexa contadorhexa_1 (
    .Rst(in_1), .C(in_2), .QA(contadorhexa_1_qa), .QB(contadorhexa_1_qb), .QC(contadorhexa_1_qc),
    .QD(contadorhexa_1_qd));
  decodificador7segmentos decodificador7segmentos_1 (
    .d0(contadorhexa_1_qa), .d1(contadorhexa_1_qb), .d2(contadorhexa_1_qc), .d3(contadorhexa_1_qd),
    .a(decodificador7segmentos_1_a), .b(decodificador7segmentos_1_b), .c(decodificador7segmentos_1_c),
    .d(decodificador7segmentos_1_d), .e(decodificador7segmentos_1_e), .f(decodificador7segmentos_1_f),
    .g(decodificador7segmentos_1_g));
  Seven_Seg seven_seg_1 (
    .a(decodificador7segmentos_1_a), .b(decodificador7segmentos_1_b), .c(decodificador7segmentos_1_c),
    .d(decodificador7segmentos_1_d), .e(decodificador7segmentos_1_e), .f(decodificador7segmentos_1_f),
    .g(decodificador7segmentos_1_g), .dp(1'b0));
endmodule
