// Digital circuit TesteDriverMAX7219.dig as structural Verilog
module TesteDriverMAX7219 (
  input  CLK50,
  output DO,
  output CS,
  output CLKout
);

  wire div8ff_1_p2;

  // Div8FF div8ff_1: pin names not known; wires that end beside it: CLK50, div8ff_1_p2
  Driver_MAX7219 driver_max7219_1 (
    .CLK(div8ff_1_p2), .Dig0(4'b0001), .Dig1(4'b0010), .Dig2(4'b0011), .Dig3(4'b0100), .Dig4(4'b0101),
    .Dig5(4'b0110), .Dig6(4'b0111), .Dig7(4'b1000), .Brilho(4'b0100), .DO(DO), .CS(CS), .CLKout(CLKout));

  // Notes on the sheet:
  //   CLK50: pin 12
  //   DO: pin 35
  //   CS: pin 33
  //   CLKout: pin 37
endmodule
