// Digital circuit TesteDriverMAX7219Hex.dig as structural Verilog
module TesteDriverMAX7219Hex (
  input  CLK50,
  output DO,
  output CS,
  output CLKout
);

  wire div8ff_1_clk_out;

  Div8FF div8ff_1 (.CLK_in(CLK50), .CLK_out(div8ff_1_clk_out));
  DriverMAX7219Hex drivermax7219hex_1 (
    .CLK(div8ff_1_clk_out), .Dig0(4'b1001), .Dig1(4'b1010), .Dig2(4'b1011), .Dig3(4'b1100), .Dig4(4'b1101),
    .Dig5(4'b1110), .Dig6(4'b1111), .Dig7(4'b1000), .Brilho(4'b0001), .DO(DO), .CS(CS), .CLKout(CLKout));

  // Notes on the sheet:
  //   CLK50: pin 12
  //   DO: pin 35
  //   CS: pin 33
  //   CLKout: pin 37
endmodule
