// Digital circuit TesteDriverMAX7219_8x8.dig as structural Verilog
module TesteDriverMAX7219_8x8 (
  input  CLK50,
  output DO,
  output CS,
  output CLKout
);

  wire div8ff_1_clk_out;
  wire [2:0] counter_1_out;
  wire [7:0] r1_d;

  Counter #(.Bits(3)) counter_1 (.en(1'b1), .C(~div8ff_1_clk_out), .clr(1'b0), .out(counter_1_out));  // open: ovf
  Div8FF div8ff_1 (.CLK_in(CLK50), .CLK_out(div8ff_1_clk_out));
  ROM #(.AddrBits(3), .Bits(8)) r1 (.A(counter_1_out), .sel(1'b1), .D(r1_d));
  DriverMAX7219_8x8 drivermax7219_8x8_1 (
    .CLK(div8ff_1_clk_out), .Brilho(4'b1111), .D(r1_d), .Addr(counter_1_out), .DO(DO), .CS(CS),
    .CLKout(CLKout));
  LedMatrix #(.ledPersistence("true")) ledmatrix_1 (.rows(r1_d), .column(counter_1_out));

  // Notes on the sheet:
  //   CLK50: pin 12, Hz: 256
  //   DO: pin 35
  //   CS: pin 33
  //   CLKout: pin 37
  //   contents of r1 (hex, n*v repeats v):
  //   9f,0,9f,5,85,e,91,11
endmodule
