// Digital circuit TestePI.dig as structural Verilog
module TestePI (
  input  CLK_50,
  input  Data_in,
  output PWM_out,
  output CLK_out,
  output CS,
  output S_out
);

  wire Clk_PI, comparator_1_lt, comparator_2_lt, divisor_1_clkout, txserial_1_buzy;
  wire [7:0] AD_data;
  wire [15:0] counter_1_out, MV;
  wire [16:0] pi_1_mv;
  wire [16:16] add_1_s;

  LeitorADC0831 leitoradc0831_1 (.clock_50(CLK_50), .Din(Data_in), .clock_out(CLK_out), .CS(CS), .AD_data(AD_data));
  Divisor divisor_1 (.ClkIn(CLK_50), .div(25'h516), .ClkOut(divisor_1_clkout));
  Counter #(.Bits(16)) counter_1 (.en(1'b1), .C(CLK_50), .clr(1'b0), .out(counter_1_out));  // open: ovf
  PI pi_1 (
    .SP(8'h32), .PV(AD_data), .KP(16'h3e8), .CLK_I(CLK_50), .ClkDiv(25'h4c4b40),
    .MV({pi_1_mv[16], pi_1_mv[14:0]}), .ClkPI(Clk_PI));
  Comparator #(.Bits(16)) comparator_1 (.a(counter_1_out), .b(MV), .lt(comparator_1_lt));  // open: gt, eq
  Comparator #(.Bits(8)) comparator_2 (.a(AD_data), .b(8'h50), .lt(comparator_2_lt));  // open: gt, eq
  and and_1 (PWM_out, comparator_1_lt, comparator_2_lt);
  TxSerial txserial_1 (
    .Transmit(Clk_PI), .Data_in(MV[15:8]), .Clock(divisor_1_clkout), .S_out(S_out), .Buzy(txserial_1_buzy));
  Add #(.Bits(17)) add_1 (
    .a({{2{pi_1_mv[16]}}, pi_1_mv[14:0]}), .b(17'h8000), .c_i(1'b0), .s({add_1_s[16], MV}));  // open: c_o

  // Other names for the same wires on the sheet: clk = CLK_50

  // Notes on the sheet:
  //   CLK_50: Hz: 5000
  //   19200 bps
  //   1302
endmodule
