// Digital circuit TesteSerialTx.dig as structural Verilog
module TesteSerialTx (
  input  CLK_50,
  output saida,
  output b
);

  wire divisor_1_clkout, not_1_out;
  wire [3:0] counter_1_out;
  wire [7:0] dados_d;

  Counter #(.Bits(4)) counter_1 (.en(1'b1), .C(~b), .clr(1'b0), .out(counter_1_out));  // open: ovf
  not not_1 (not_1_out, b);
  Divisor divisor_1 (.ClkIn(CLK_50), .div(25'ha2c), .ClkOut(divisor_1_clkout));
  ROM #(.AddrBits(4), .Bits(8)) dados (.A(counter_1_out), .sel(1'b1), .D(dados_d));
  TxSerial txserial_1 (.Transmit(not_1_out), .Data_in(dados_d), .Clock(divisor_1_clkout), .S_out(saida), .Buzy(b));

  // Notes on the sheet:
  //   2604 para 9600 bps
  //   contents of dados (hex, n*v repeats v):
  //   4b,65,72,73,63,68,62,61,75,6d,65,72,2e,2e,2e,d
endmodule
