// Digital circuit TetTecMatCPLD.dig as structural Verilog
module TetTecMatCPLD (
  input  CLK50,
  input  C0,
  input  C1,
  input  C2,
  input  C3,
  output a,
  output b,
  output c,
  output d,
  output e,
  output f,
  output g,
  output L1,
  output L2,
  output L3,
  output L4
);

  wire div8ff_1_clk_out, div8ff_2_clk_out, letecmat4x4_1_kp, letecmat4x4_1_q0, letecmat4x4_1_q1,
       letecmat4x4_1_q2, letecmat4x4_1_q3;
  wire [3:0] d_ff_1_q, r1_d;

  Div8FF div8ff_1 (.CLK_in(CLK50), .CLK_out(div8ff_1_clk_out));
  Div8FF div8ff_2 (.CLK_in(div8ff_1_clk_out), .CLK_out(div8ff_2_clk_out));
  LeTecMat4x4 letecmat4x4_1 (
    .clk(div8ff_2_clk_out), .L0(L1), .L1(L2), .L2(L3), .L3(L4), .C0(C0), .C1(C1), .C2(C2), .C3(C3),
    .Q0(letecmat4x4_1_q0), .Q1(letecmat4x4_1_q1), .Q2(letecmat4x4_1_q2), .Q3(letecmat4x4_1_q3),
    .Kp(letecmat4x4_1_kp));
  D_FF d_ff_1 (.D(letecmat4x4_1_q0), .C(letecmat4x4_1_kp), .Q(d_ff_1_q[0]));  // open: nQ
  D_FF d_ff_2 (.D(letecmat4x4_1_q1), .C(letecmat4x4_1_kp), .Q(d_ff_1_q[1]));  // open: nQ
  D_FF d_ff_3 (.D(letecmat4x4_1_q2), .C(letecmat4x4_1_kp), .Q(d_ff_1_q[2]));  // open: nQ
  D_FF d_ff_4 (.D(letecmat4x4_1_q3), .C(letecmat4x4_1_kp), .Q(d_ff_1_q[3]));  // open: nQ
  ROM #(.AddrBits(4), .Bits(4)) r1 (.A(d_ff_1_q), .sel(1'b1), .D(r1_d));
  decodificador7segmentos decodificador7segmentos_1 (
    .d0(r1_d[0]), .d1(r1_d[1]), .d2(r1_d[2]), .d3(r1_d[3]), .a(a), .b(b), .c(c), .d(d), .e(e), .f(f), .g(g));

  // Notes on the sheet:
  //   contents of r1 (hex, n*v repeats v):
  //   1,2,3,a,4,5,6,b,7,8,9,c,e,0,f,d
endmodule
