// Digital circuit TxSerial.dig as structural Verilog
module TxSerial (
  input  Transmit,
  input  [7:0] Data_in,
  input  Clock,
  output S_out,
  output Buzy
);

  wire and_1_out, comparator_1_eq, d_ff_as_1_nq;
  wire [3:0] cont4_1_q;
  wire [7:0] register_1_q;

  and and_1 (and_1_out, Transmit, d_ff_as_1_nq);
  Register #(.Bits(8)) register_1 (.D(Data_in), .C(and_1_out), .en(1'b1), .Q(register_1_q));
  D_FF_AS d_ff_as_1 (.Set(1'b0), .D(d_ff_as_1_nq), .C(and_1_out), .Clr(comparator_1_eq), .Q(Buzy), .nQ(d_ff_as_1_nq));
  cont4 cont4_1 (.clock(Clock), .Reset(d_ff_as_1_nq), .Q(cont4_1_q));
  Multiplexer #(.Selector_Bits(4)) multiplexer_1 (
    .sel(cont4_1_q), .in_0(1'b1), .in_1(1'b0), .in_2(register_1_q[0]), .in_3(register_1_q[1]),
    .in_4(register_1_q[2]), .in_5(register_1_q[3]), .in_6(register_1_q[4]), .in_7(register_1_q[5]),
    .in_8(register_1_q[6]), .in_9(register_1_q[7]), .in_10(1'b1), .in_11(1'b1), .in_12(1'b1), .in_13(1'b1),
    .in_14(1'b1), .in_15(1'b1), .out(S_out));
  Comparator #(.Bits(4)) comparator_1 (.a(cont4_1_q), .b(4'b1011), .eq(comparator_1_eq));  // open: gt, lt

  // Notes on the sheet:
  //   S_out: Saida serial
endmodule
