// Digital circuit VGA.dig as structural Verilog
module VGA (
  input  CLK50,
  output HS,
  output VS
);

  wire CLK25;
  wire [9:0] vgatiming_1_hcounter;

  VgaTiming vgatiming_1 (
    .CLK50(CLK50), .HS(HS), .VS(VS), .HCounter(vgatiming_1_hcounter), .CLK25(CLK25));  // open: Valid, VCounter
  VGA vga_1 (
    .R(vgatiming_1_hcounter[6]), .G(vgatiming_1_hcounter[7]), .B(vgatiming_1_hcounter[8]), .H(HS), .V(VS),
    .C(CLK25));

  // Notes on the sheet:
  //   CLK50: Hz: 50000000
endmodule
