// Digital circuit VGA800x600_60.dig as structural Verilog
module VGA800x600_60 (
  input  CLK40,
  output HS,
  output VS,
  output [10:0] HCounter,
  output [9:0] VCounter
);

  wire and_1_out, comparator_1_gt, comparator_2_lt, comparator_3_eq, comparator_4_eq, comparator_5_gt,
       comparator_6_lt;

  and and_1 (and_1_out, comparator_3_eq, comparator_4_eq);
  Counter #(.Bits(11)) u_HCounter (.en(1'b1), .C(CLK40), .clr(comparator_3_eq), .out(HCounter));  // open: ovf
  Counter #(.Bits(10)) u_VCounter (.en(comparator_3_eq), .C(CLK40), .clr(and_1_out), .out(VCounter));  // open: ovf
  Comparator #(.Bits(11)) comparator_1 (.a(HCounter), .b(11'h376), .gt(comparator_1_gt));  // open: eq, lt
  Comparator #(.Bits(11)) comparator_2 (.a(HCounter), .b(11'h3f7), .lt(comparator_2_lt));  // open: gt, eq
  Comparator #(.Bits(11)) comparator_3 (.a(HCounter), .b(11'h41f), .eq(comparator_3_eq));  // open: gt, lt
  Comparator #(.Bits(10)) comparator_4 (.a(VCounter), .b(10'h273), .eq(comparator_4_eq));  // open: gt, lt
  Comparator #(.Bits(10)) comparator_5 (.a(VCounter), .b(10'h26c), .gt(comparator_5_gt));  // open: eq, lt
  Comparator #(.Bits(10)) comparator_6 (.a(VCounter), .b(10'h271), .lt(comparator_6_lt));  // open: gt, eq
  nand nand_1 (HS, comparator_1_gt, comparator_2_lt);
  nand nand_2 (VS, comparator_5_gt, comparator_6_lt);
  // Pins of 10 and 11 bits meet at HCounter

  // Notes on the sheet:
  //   CLK40: Hz: 40000000
endmodule
