// Digital circuit VGA_TXT.dig as structural Verilog
module VGA_TXT (
  input  CLK25175,
  output HS,
  output VS,
  output R,
  output G,
  output B
);

  wire comparator_1_gt;
  wire [9:0] vga800x600_60_1_vcounter;

  VGA800x600_60 vga800x600_60_1 (
    .CLK40(CLK25175), .HS(HS), .VS(VS), .VCounter(vga800x600_60_1_vcounter));  // open: HCounter
  Comparator #(.Bits(10)) comparator_1 (
    .a(vga800x600_60_1_vcounter), .b(10'h96), .gt(comparator_1_gt));  // open: eq, lt
  Multiplexer multiplexer_1 (.sel(comparator_1_gt), .in_0(1'b0), .in_1(1'b1), .out(R));
  Multiplexer multiplexer_2 (.sel(comparator_1_gt), .in_0(1'b0), .in_1(1'b0), .out(G));
  Multiplexer multiplexer_3 (.sel(comparator_1_gt), .in_0(1'b0), .in_1(1'b0), .out(B));
  VGA vga_1 (.R(R), .G(G), .B(B), .H(HS), .V(VS), .C(CLK25175));

  // Notes on the sheet:
  //   CLK25175: Hz: 40000000
endmodule
