// Digital circuit VgaTiming.dig as structural Verilog
module VgaTiming (
  input  CLK50,
  output HS,
  output VS,
  output Valid,
  output [9:0] HCounter,
  output [9:0] VCounter,
  output CLK25
);

  wire and_1_out, CLK_2_nq, comparator_1_lt, comparator_2_gt, comparator_3_lt, comparator_4_eq,
       comparator_5_lt, comparator_6_eq, comparator_7_gt, comparator_8_lt;

  D_FF CLK_2 (.D(CLK_2_nq), .C(CLK50), .Q(CLK25), .nQ(CLK_2_nq));
  and and_1 (and_1_out, comparator_4_eq, comparator_6_eq);
  Counter #(.Bits(10)) u_HCounter (.en(1'b1), .C(CLK25), .clr(comparator_4_eq), .out(HCounter));  // open: ovf
  Counter #(.Bits(10)) u_VCounter (.en(comparator_4_eq), .C(CLK25), .clr(and_1_out), .out(VCounter));  // open: ovf
  Comparator #(.Bits(10)) comparator_1 (.a(HCounter), .b(10'h280), .lt(comparator_1_lt));  // open: gt, eq
  Comparator #(.Bits(10)) comparator_2 (.a(HCounter), .b(10'h28e), .gt(comparator_2_gt));  // open: eq, lt
  Comparator #(.Bits(10)) comparator_3 (.a(HCounter), .b(10'h2ef), .lt(comparator_3_lt));  // open: gt, eq
  Comparator #(.Bits(10)) comparator_4 (.a(HCounter), .b(10'h31f), .eq(comparator_4_eq));  // open: gt, lt
  Comparator #(.Bits(10)) comparator_5 (.a(VCounter), .b(10'h1e0), .lt(comparator_5_lt));  // open: gt, eq
  Comparator #(.Bits(10)) comparator_6 (.a(VCounter), .b(10'h20c), .eq(comparator_6_eq));  // open: gt, lt
  Comparator #(.Bits(10)) comparator_7 (.a(VCounter), .b(10'h1e9), .gt(comparator_7_gt));  // open: eq, lt
  Comparator #(.Bits(10)) comparator_8 (.a(VCounter), .b(10'h1ec), .lt(comparator_8_lt));  // open: gt, eq
  nand nand_1 (HS, comparator_2_gt, comparator_3_lt);
  and and_2 (Valid, comparator_1_lt, comparator_5_lt);
  nand nand_2 (VS, comparator_7_gt, comparator_8_lt);

  // Notes on the sheet:
  //   CLK50: Hz: 50350000
  //   489
endmodule
