// Digital circuit cont4.dig as structural Verilog
module cont4 (
  input  clock,
  input  Reset,
  output [3:0] Q
);

  wire d_ff_as_1_nq, d_ff_as_2_nq, d_ff_as_3_nq, d_ff_as_4_nq;

  D_FF_AS d_ff_as_1 (.Set(1'b0), .D(d_ff_as_1_nq), .C(clock), .Clr(Reset), .Q(Q[0]), .nQ(d_ff_as_1_nq));
  D_FF_AS d_ff_as_2 (.Set(1'b0), .D(d_ff_as_2_nq), .C(d_ff_as_1_nq), .Clr(Reset), .Q(Q[1]), .nQ(d_ff_as_2_nq));
  D_FF_AS d_ff_as_3 (.Set(1'b0), .D(d_ff_as_3_nq), .C(d_ff_as_2_nq), .Clr(Reset), .Q(Q[2]), .nQ(d_ff_as_3_nq));
  D_FF_AS d_ff_as_4 (.Set(1'b0), .D(d_ff_as_4_nq), .C(d_ff_as_3_nq), .Clr(Reset), .Q(Q[3]), .nQ(d_ff_as_4_nq));
endmodule
