// Digital circuit cont8.dig as structural Verilog
module cont8 (
  input  clock,
  input  Reset,
  output [7:0] Q
);

  wire d_ff_as_1_nq, d_ff_as_2_nq, d_ff_as_3_nq, d_ff_as_4_nq, d_ff_as_5_nq, d_ff_as_6_nq, d_ff_as_7_nq,
       d_ff_as_8_nq;

  D_FF_AS d_ff_as_1 (.Set(1'b0), .D(d_ff_as_1_nq), .C(clock), .Clr(Reset), .Q(Q[0]), .nQ(d_ff_as_1_nq));
  D_FF_AS d_ff_as_2 (.Set(1'b0), .D(d_ff_as_2_nq), .C(d_ff_as_1_nq), .Clr(Reset), .Q(Q[1]), .nQ(d_ff_as_2_nq));
  D_FF_AS d_ff_as_3 (.Set(1'b0), .D(d_ff_as_3_nq), .C(d_ff_as_2_nq), .Clr(Reset), .Q(Q[2]), .nQ(d_ff_as_3_nq));
  D_FF_AS d_ff_as_4 (.Set(1'b0), .D(d_ff_as_4_nq), .C(d_ff_as_3_nq), .Clr(Reset), .Q(Q[3]), .nQ(d_ff_as_4_nq));
  D_FF_AS d_ff_as_5 (.Set(1'b0), .D(d_ff_as_5_nq), .C(d_ff_as_4_nq), .Clr(Reset), .Q(Q[4]), .nQ(d_ff_as_5_nq));
  D_FF_AS d_ff_as_6 (.Set(1'b0), .D(d_ff_as_6_nq), .C(d_ff_as_5_nq), .Clr(Reset), .Q(Q[5]), .nQ(d_ff_as_6_nq));
  D_FF_AS d_ff_as_7 (.Set(1'b0), .D(d_ff_as_7_nq), .C(d_ff_as_6_nq), .Clr(Reset), .Q(Q[6]), .nQ(d_ff_as_7_nq));
  D_FF_AS d_ff_as_8 (.Set(1'b0), .D(d_ff_as_8_nq), .C(d_ff_as_7_nq), .Clr(Reset), .Q(Q[7]), .nQ(d_ff_as_8_nq));
endmodule
