// Digital circuit decodificador7segmentos.dig as structural Verilog
module decodificador7segmentos (
  input  d0,
  input  d1,
  input  d2,
  input  d3,
  output a,
  output b,
  output c,
  output d,
  output e,
  output f,
  output g
);

  ROM #(.AddrBits(4), .Bits(7)) rom (.A({d3, d2, d1, d0}), .sel(1'b1), .D({g, f, e, d, c, b, a}));

  // Notes on the sheet:
  //   contents of rom (hex, n*v repeats v):
  //   3f,6,5b,4f,66,6d,7d,7,7f,67,77,7c,39,5e,79,71
endmodule
