// Digital circuit teste4511.dig as structural Verilog
module teste4511 (
  input  [3:0] in_1,
  input  in_2,
  input  in_3,
  input  in_4
);

  wire cd4511_1_p10, cd4511_1_p11, cd4511_1_p12, cd4511_1_p13, cd4511_1_p14, cd4511_1_p15, cd4511_1_p16;

  // CD4511 cd4511_1: pin names not known; wires that end beside it: in_1[1], in_1[2], in_2, in_3, in_4, in_1[3], in_1[0], 1'b0, 1'b1, cd4511_1_p10, cd4511_1_p11, cd4511_1_p12, cd4511_1_p13, cd4511_1_p14, cd4511_1_p15, cd4511_1_p16
  Seven_Seg seven_seg_1 (
    .a(cd4511_1_p12), .b(cd4511_1_p13), .c(cd4511_1_p14), .d(cd4511_1_p15), .e(cd4511_1_p16),
    .f(cd4511_1_p10), .g(cd4511_1_p11), .dp(1'b0));
endmodule
